# Fritzing sketch Untitled Sketch (saved by Fritzing 0.9.5d)
breadboards: 1

parts:
  A1 = illuminated SPDT push button switch
  VCC1 = Battery
  M1 = DC Motor

nets:
  N1: A1.Pin_1, M1.pin_1
  N2: A1.Pin_3, VCC1.+
  N3: VCC1.-, M1.pin_2

custom parts:
  illuminated SPDT push button switch: illuminated SPDT push button switch.
